# Fritzing sketch ELRS Surface Reciever2 (saved by Fritzing 1.0.1rc)
circuit board: 3.7cm x 4.5cm
perfboards: 1

parts:
  NPN_TRANSISTOR_ARRAY = ULN2003A [package="DIP16 [THT]"]
  ELRS_EP2 = ELRS EP2 Receiver
  J4_LED_GND = male pin header, 6 pins [form="♂ (male)"]
  J5_LED_5V = male pin header, 6 pins [form="♂ (male)"]
  J3_SERVO_PWM = male pin header, 6 pins [form="♂ (male)"]
  J2_SERVO_5V = male pin header, 6 pins [form="♂ (male)"]
  Waveshare = Waveshare rp2040-zero tht [package=THT]
  J1_SERVO_GND = male pin header, 6 pins [form="♂ (male)"]
  J6_Blank = male pin header, 6 pins [form="♂ (male)"]  # not connected

nets:
  N1: NPN_TRANSISTOR_ARRAY.In_1, NPN_TRANSISTOR_ARRAY.In_2, Waveshare.Pin_21
  N2: NPN_TRANSISTOR_ARRAY.In_3, Waveshare.Pin_20
  N3: NPN_TRANSISTOR_ARRAY.In_4, Waveshare.Pin_19
  N4: NPN_TRANSISTOR_ARRAY.In_5, Waveshare.Pin_18
  N5: NPN_TRANSISTOR_ARRAY.In_6, Waveshare.Pin_17
  N6: NPN_TRANSISTOR_ARRAY.In_7, Waveshare.Pin_16
  N7: NPN_TRANSISTOR_ARRAY.0V, ELRS_EP2.GND, Waveshare.Pin_2, J1_SERVO_GND.pin1, J1_SERVO_GND.pin2, J1_SERVO_GND.pin3, J1_SERVO_GND.pin4, J1_SERVO_GND.pin5, J1_SERVO_GND.pin6
  N8: NPN_TRANSISTOR_ARRAY.COM_-_Common, ELRS_EP2.5V, J5_LED_5V.pin1, J5_LED_5V.pin2, J5_LED_5V.pin3, J5_LED_5V.pin4, J5_LED_5V.pin5, J5_LED_5V.pin6, J2_SERVO_5V.pin1, J2_SERVO_5V.pin2, J2_SERVO_5V.pin3, J2_SERVO_5V.pin4, J2_SERVO_5V.pin5, J2_SERVO_5V.pin6, Waveshare.Pin_1
  N9: NPN_TRANSISTOR_ARRAY.Out_7, J4_LED_GND.pin1
  N10: NPN_TRANSISTOR_ARRAY.Out_6, J4_LED_GND.pin2
  N11: NPN_TRANSISTOR_ARRAY.Out_5, J4_LED_GND.pin3
  N12: NPN_TRANSISTOR_ARRAY.Out_4, J4_LED_GND.pin4
  N13: NPN_TRANSISTOR_ARRAY.Out_3, J4_LED_GND.pin5
  N14: NPN_TRANSISTOR_ARRAY.Out_2, NPN_TRANSISTOR_ARRAY.Out_1, J4_LED_GND.pin6
  N15: ELRS_EP2.RX, Waveshare.Pin_15
  N16: ELRS_EP2.TX, Waveshare.Pin_14
  N17: J3_SERVO_PWM.pin1, Waveshare.Pin_9
  N18: J3_SERVO_PWM.pin2, Waveshare.Pin_8
  N19: J3_SERVO_PWM.pin3, Waveshare.Pin_7
  N20: J3_SERVO_PWM.pin4, Waveshare.Pin_6
  N21: J3_SERVO_PWM.pin5, Waveshare.Pin_5
  N22: J3_SERVO_PWM.pin6, Waveshare.Pin_4

notes:
  RP2040 Zero
  Receiver
  <-- 0.5A Digital Switch
  <-- Servo PWM
  Connection

custom parts:
  ELRS EP2 Receiver: ELRS EP2 Receiver by HappyModel
  Waveshare rp2040-zero tht: .RP2040-Zero, A Low-Cost, High-Performance Pico-Like MCU Board Based On Raspberry Pi Microcontroller RP2040. This varant is THT without the extra connections.
